# Fritzing sketch light-wireup (saved by Fritzing 0.9.3b)

parts:
  U1 = NodeMCU
  Part1 = NeoPixel NeoMatrix 8x8 [part_number=1487]

nets:
  N1: U1.connector0, Part1.IN
  N2: U1.connector15, Part1.VDD
  N3: U1.connector16, Part1.GND

custom parts:
  NeoPixel NeoMatrix 8x8: Put on your sunglasses before wiring up this LED matrix - 64 eye-blistering RGB LEDs adorn the NeoMatrix for a blast of configurable color. Arranged in an 8x8 matrix, each pixel is individually addressable. Only one microcontroller pin is required to control all the LEDs, and you get 24 bit color for each LED.
